# Fritzing sketch Ampelsteuerung (saved by Fritzing 0.9.3b)
breadboards: 1

parts:
  Bauteil1 = Arduino Uno (Rev3)
  Ampel1Taster = Pushbutton [package="[THT]"]
  Ampel2Taster = Pushbutton [package="[THT]"]
  Ampel2Gruen2 = LED - 3mm [color="Green (570nm)" package="3 mm [THT]"]
  Ampel2Rot2 = LED - 3mm [color="Red (633nm)" package="3 mm [THT]"]
  Ampel1Gruen1 = LED - 3mm [color="Green (555nm)" package="3 mm [THT]"]
  Ampel1Rot1 = LED - 3mm [color="Red (633nm)" package="3 mm [THT]"]
  Ampel1Gelb1 = LED - 3mm [color="Yellow (574nm)" package="3 mm [THT]"]
  Ampel1Rot2 = LED - 3mm [color="Red (633nm)" package="3 mm [THT]"]
  Ampel1Gruen2 = LED - 3mm [color="Green (570nm)" package="3 mm [THT]"]
  Ampel2Rot1 = LED - 3mm [color="Red (633nm)" package="3 mm [THT]"]
  Ampel2Gelb1 = LED - 3mm [color="Yellow (595nm)" package="3 mm [THT]"]
  Ampel2Gruen1 = LED - 3mm [color="Green (570nm)" package="3 mm [THT]"]
  R1 = Resistor [tolerance=±5% resistance=150 package=THT]
  R2 = Resistor [tolerance=±5% resistance=150 package=THT]
  R3 = Resistor [tolerance=±5% resistance=150 package=THT]
  R4 = Resistor [tolerance=±5% resistance=150 package=THT]
  R5 = Resistor [tolerance=±5% resistance=150 package=THT]
  R6 = Resistor [tolerance=±5% resistance=150 package=THT]
  R7 = Resistor [tolerance=±5% resistance=150 package=THT]
  R8 = Resistor [tolerance=±5% resistance=150 package=THT]
  R9 = Resistor [tolerance=±5% resistance=150 package=THT]
  R10 = Resistor [tolerance=±5% resistance=150 package=THT]

nets (from the schematic view):
  N1: Bauteil1.D8, R9.Pin_0
  N2: Bauteil1.D9_PWM, R10.Pin_0
  N3: Bauteil1.D12/MISO, Ampel1Taster.Pin_2
  N4: Bauteil1.D13/SCK, Bauteil1.5V, Ampel1Taster.Pin_3, Ampel1Taster.Pin_4, Ampel2Taster.Pin_1, Ampel2Taster.Pin_3, Ampel2Taster.Pin_4
  N5: Bauteil1.GND, Ampel2Gruen2.cathode, Ampel2Rot2.cathode, Ampel1Gruen1.cathode, Ampel1Rot1.cathode, Ampel1Gelb1.cathode, Ampel1Rot2.cathode, Ampel1Gruen2.cathode, Ampel2Rot1.cathode, Ampel2Gelb1.cathode, Ampel2Gruen1.cathode
  N6: Bauteil1.D0/RX, R1.Pin_0
  N7: Bauteil1.D1/TX, R2.Pin_0
  N8: Bauteil1.D2, R3.Pin_0
  N9: Bauteil1.D3_PWM, R4.Pin_0
  N10: Bauteil1.D4, R5.Pin_0
  N11: Bauteil1.D5_PWM, R6.Pin_0
  N12: Bauteil1.D6_PWM, R7.Pin_0
  N13: Bauteil1.D7, R8.Pin_0
  N14: Ampel2Gruen2.anode, R10.Pin_1
  N15: Ampel2Rot2.anode, R9.Pin_1
  N16: Ampel1Gruen1.anode, R3.Pin_1
  N17: Ampel1Rot1.anode, R1.Pin_1
  N18: Ampel1Gelb1.anode, R2.Pin_1
  N19: Ampel1Rot2.anode, R5.Pin_1
  N20: Ampel1Gruen2.anode, R4.Pin_1
  N21: Ampel2Rot1.anode, R6.Pin_1
  N22: Ampel2Gelb1.anode, R7.Pin_1
  N23: Ampel2Gruen1.anode, R8.Pin_1

// code stored in the sketch: Ampelsteuerung.ino
int ampel1red1 = 0;
int ampel1yellow1 = 1;
int ampel1green1 = 2;
#define ampel1red2  3;
#define ampel1green2 4
#define ampel2red1 5
#define ampel2yellow1 6
int ampel2green1 = 7;
int ampel2red2 = 8;
int ampel2green2 = 9;
int ampel1Taster = 12;
int ampel2Taster = 13;


void setup(){
	pinMode(ampel1red1,OUTPUT);
	pinMode(ampel1yellow1,OUTPUT);
	pinMode(ampel1green1,OUTPUT);
	pinMode(ampel1red2,OUTPUT);
	pinMode(ampel1green2,OUTPUT);
	pinMode(ampel2red1,OUTPUT);
	pinMode(ampel2yellow1,OUTPUT);
	pinMode(ampel2green1,OUTPUT);
	pinMode(ampel2red2,OUTPUT);
	pinMode(ampel2green2,OUTPUT);
	pinMode(ampel1Taster,INPUT);
	pinMode(ampel2Taster,INPUT);
}

void loop(){
	
}
